// Logisim project parte1_cache.circ as structural Verilog: 1 circuit, main circuit main
module main (
  input  [5:0] ENDERECO,
  input  RESET,
  input  CLK,
  output out_4
);

  wire and_1_out, and_2_out, and_3_out, and_4_out, and_5_out, and_6_out, and_7_out, d_ff_1_q, d_ff_2_q,
       d_ff_3_q, d_ff_4_q, multiplexer_1_out, not_1_out, not_2_out, not_3_out, not_4_out, not_5_out,
       not_6_out, not_7_out, or_1_out, or_2_out, or_3_out, or_4_out;
  wire [2:0] MEMORIA_ROTULOS_dout;
  wire [3:0] counter_1_q;

  D_Flip_Flop d_ff_1 (.D(1'b1), .clk(CLK), .Q(d_ff_1_q), .reset(RESET));  // open: Qn, preset
  D_Flip_Flop d_ff_2 (.D(1'b1), .clk(CLK), .Q(d_ff_2_q), .reset(RESET));  // open: Qn, preset
  D_Flip_Flop d_ff_3 (.D(1'b1), .clk(CLK), .Q(d_ff_3_q), .reset(RESET));  // open: Qn, preset
  D_Flip_Flop d_ff_4 (.D(1'b1), .clk(CLK), .Q(d_ff_4_q), .reset(RESET));  // open: Qn, preset
  RAM #(.addrWidth(2), .dataWidth(3)) MEMORIA_ROTULOS (
    .addr(ENDERECO[2:1]), .clk(CLK), .dout(MEMORIA_ROTULOS_dout));  // open: we, oe, din
  Multiplexer #(.select(2)) multiplexer_1 (
    .in0(d_ff_1_q), .in1(d_ff_2_q), .in2(d_ff_3_q), .in3(d_ff_4_q), .out(multiplexer_1_out),
    .sel(ENDERECO[2:1]));
  LED led_1 (.in(ENDERECO[0]));
  not not_1 (not_1_out, ENDERECO[3]);
  and and_1 (and_1_out, not_1_out, MEMORIA_ROTULOS_dout[0]);
  not not_2 (not_2_out, MEMORIA_ROTULOS_dout[0]);
  and and_2 (and_2_out, not_2_out, ENDERECO[3]);
  not not_3 (not_3_out, ENDERECO[4]);
  and and_3 (and_3_out, not_3_out, MEMORIA_ROTULOS_dout[1]);
  not not_4 (not_4_out, MEMORIA_ROTULOS_dout[1]);
  and and_4 (and_4_out, not_4_out, ENDERECO[4]);
  not not_5 (not_5_out, ENDERECO[5]);
  and and_5 (and_5_out, not_5_out, MEMORIA_ROTULOS_dout[2]);
  not not_6 (not_6_out, MEMORIA_ROTULOS_dout[2]);
  and and_6 (and_6_out, not_6_out, ENDERECO[5]);
  or or_1 (or_1_out, and_1_out, and_2_out);
  or or_2 (or_2_out, and_3_out, and_4_out);
  or or_3 (or_3_out, or_1_out, or_2_out, or_4_out);
  or or_4 (or_4_out, and_5_out, and_6_out);
  not not_7 (not_7_out, or_3_out);
  and and_7 (and_7_out, not_7_out, multiplexer_1_out);
  Counter #(.max('hf), .width(4)) counter_1 (.Q(counter_1_q), .clk(and_7_out));  // open: load, D, count, carry, up, clr
  Hex_Digit_Display hex_digit_display_1 (.value(counter_1_q));  // open: dp

  assign out_4 = ENDERECO[0];
endmodule
